# Fritzing sketch esquema_motor_puenteH (saved by Fritzing 0.9.3b)
breadboards: 1

parts:
  U1 = Optocoupler [package=THT]
  Componente1 = Arduino Uno (Rev3) - ICSP
  R1 = Resistor [tolerance=±5% resistance=330 package="0402 [SMD]"]
  M1 = DC Motor
  R3 = Resistor [tolerance=±5% resistance=10k package="2010 [SMD]"]
  R4 = Resistor [tolerance=±5% resistance=10k package="2010 [SMD]"]
  Q7 = Basic FET N-Channel [package="DPak [SMD]"]
  Q8 = Basic FET N-Channel [package="DPak [SMD]"]
  Q6 = Basic FET P-Channel [package="DPak [SMD]"]
  Q5 = Basic FET P-Channel [package="DPak [SMD]"]
  R5 = Resistor [tolerance=±5% resistance=330 package="0402 [SMD]"]
  U2 = Optocoupler [package=THT]
  VCC1 = Battery block 9V

nets:
  N1: U1.Pin_1, Componente1.D6_PWM, R1.Pin_0, R1.Pin_1
  N2: U1.Pin_2, Componente1.GND, U2.Pin_2
  N3: U1.Pin_4, Q7.source, Q8.source, U2.Pin_4, VCC1.-
  N4: U1.Pin_5, R4.Pin_1, Q8.drain, Q5.drain
  N5: Componente1.D5_PWM, R5.Pin_0, R5.Pin_1, U2.Pin_1
  N6: M1.pin_1, Q8.Gate, Q5.Gate
  N7: M1.pin_2, Q7.Gate, Q6.Gate
  N8: R3.Pin_0, R4.Pin_0, Q6.source, Q5.source, VCC1.+
  N9: R3.Pin_1, Q7.drain, Q6.drain, U2.Pin_5
