# Fritzing sketch esquema_motor_puenteH_v02 (saved by Fritzing 0.9.3b)
breadboards: 1

parts:
  U1 = Optocoupler [package=THT]
  R1 = Resistor [tolerance=±5% resistance=330 package="0402 [SMD]"]
  M1 = DC Motor
  Q3 = Basic FET N-Channel [package="DPak [SMD]"]
  U2 = Optocoupler [package=THT]
  Q2 = Basic FET P-Channel [package="DPak [SMD]"]
  R3 = Resistor [tolerance=±5% resistance=1k package="0402 [SMD]"]
  R4 = Resistor [tolerance=±5% resistance=1k package="0402 [SMD]"]
  Arduino = Arduino Uno (Rev3) - ICSP
  R2 = Resistor [tolerance=±10% resistance=1k package="0402 [SMD]"]
  Q1 = Basic FET N-Channel [package="DPak [SMD]"]
  Q4 = Basic FET P-Channel [package="DPak [SMD]"]

nets:
  N1: U1.Pin_1, R1.Pin_0, R1.Pin_1, Arduino.D6_PWM
  N2: U1.Pin_2, U2.Pin_2, Arduino.GND
  GND: U1.Pin_4, Q3.source, U2.Pin_4, Q1.source
  N3: U1.Pin_5, Q2.Gate, R3.Pin_0, Q1.Gate
  N4: M1.pin_1, Q2.drain, Q1.drain
  N5: M1.pin_2, Q3.drain, Q4.drain
  N6: Q3.Gate, U2.Pin_5, R4.Pin_0, Q4.Gate
  N7: U2.Pin_1, Arduino.D5_PWM, R2.Pin_0, R2.Pin_1
  9V: Q2.source, R3.Pin_1, R4.Pin_1, Q4.source
