# Fritzing sketch esquema_motor_potenciometro (saved by Fritzing 0.9.3b)
circuit board: 8.46667cm x 5.64444cm
breadboards: 1

parts:
  U1 = Optocoupler [package=THT]
  R1 = Resistor [tolerance=±5% resistance=220 package=THT]
  Q1 = Basic FET N-Channel [package="TO220 [THT]"]
  R2 = Resistor [tolerance=±5% resistance=10k package="2010 [SMD]"]
  M1 = DC Motor
  Componente1 = Arduino Uno (Rev3)
  VCC1 = Battery block 9V
  D1 = Diode [package=diode-1n4148]
  R3 = Rotary Potentiometer (Small) [maximum_resistance=100kΩ package=THT]

nets:
  N1: U1.Pin_1, Componente1.D3_PWM
  N2: U1.Pin_2, R1.Pin_0
  N3: U1.Pin_4, Q1.gate, R2.Pin_0
  N4: U1.Pin_5, M1.pin_1, VCC1.+, D1.C
  N5: R1.Pin_1, Componente1.GND, R3.leg2
  N6: Q1.drain, M1.pin_2, D1.A
  N7: Q1.source, R2.Pin_1, VCC1.-
  N8: Componente1.A0, R3.wiper
  N9: Componente1.5V, R3.leg1
