# Fritzing sketch esquema_motor_puenteH_v01 (saved by Fritzing 0.9.3b)
breadboards: 1

parts:
  U1 = Optocoupler [package=THT]
  Componente1 = Arduino Uno (Rev3) - ICSP
  R1 = Resistor [tolerance=±5% resistance=330 package="0402 [SMD]"]
  M1 = DC Motor
  R3 = Resistor [tolerance=±5% resistance=10k package="2010 [SMD]"]
  Q7 = Basic FET N-Channel [package="DPak [SMD]"]
  Q8 = Basic FET N-Channel [package="DPak [SMD]"]
  Q6 = Basic FET P-Channel [package="DPak [SMD]"]
  R5 = Resistor [tolerance=±5% resistance=330 package="0402 [SMD]"]
  U2 = Optocoupler [package=THT]
  Q5 = Basic FET P-Channel [package="DPak [SMD]"]
  VCC1 = Battery block 9V  # not connected

nets (from the breadboard view):
  N1: U1.Pin_1, Componente1.D6_PWM, R1.Pin_0, R1.Pin_1
  N2: U1.Pin_2, Componente1.GND, Q6.source, U2.Pin_2, Q5.source
  N3: U1.Pin_4, Q8.source
  N4: U1.Pin_5, Q8.Gate, Q5.Gate
  N5: Componente1.D5_PWM, R5.Pin_0, R5.Pin_1, U2.Pin_1
  N6: M1.pin_1, Q8.drain, Q5.drain
  N7: M1.pin_2, R3.Pin_1, Q7.drain, Q6.drain
  N8: Q7.Gate, Q6.Gate, U2.Pin_5
  N9: Q7.source, U2.Pin_4
